// Logisim project Counter.circ as structural Verilog
module Counter (
  input  next,
  input  jump,
  input  clk,
  input  [17:0] \input ,
  input  reset,
  output [17:0] \output 
);

  wire load_enable, not_1_out, or_1_out;
  wire [17:0] added_value, n18_bits_inverter_1_out_2, substracted_value, value_to_load;

  not not_1 (not_1_out, next);
  and and_1 (load_enable, not_1_out, or_1_out);
  or or_1 (or_1_out, jump, \input [17]);
  Counter_part #(.width(18), .max('h3ffff)) counter_1 (
    .load(load_enable), .D(value_to_load), .count(next), .Q(\output ), .clk(clk), .clr(reset));  // open: carry
  _18_bits_inverter u_18_bits_inverter_1 (.in_1(\input ), .out_2(n18_bits_inverter_1_out_2));
  Adder #(.width(18)) adder_1 (.a(\input ), .b(\output ), .out(added_value));  // open: cin, cout
  Subtractor #(.width(18)) subtractor_1 (
    .a(\output ), .b(n18_bits_inverter_1_out_2), .out(substracted_value));  // open: bin, bout
  assign value_to_load = jump ? added_value : 18'bz;  // Controlled_Buffer controlled_buffer_1
  assign value_to_load = \input [17] ? substracted_value : 18'bz;  // Controlled_Buffer controlled_buffer_2

  // Other names for the same wires on the sheet: count = next; substract = \input [17]

  // Notes on the sheet:
  //   increment by 1 (count=1, clock ticks)
endmodule

module _18_bits_inverter (
  input  [17:0] in_1,
  output [17:0] out_2
);

  wire [17:0] negator_1_out;

  Negator #(.width(18)) negator_1 (.in(in_1), .out(negator_1_out));
  Multiplexer #(.width(18)) multiplexer_1 (.in0(in_1), .in1(negator_1_out), .out(out_2), .sel(in_1[17]));  // open: en
endmodule
