// Logisim project alu.circ as structural Verilog: 20 circuits, main circuit 2_bits_adder
module main (
  input  in_1,
  output [3:0] read_register_1,
  output [3:0] read_register_2,
  output [17:0] ALU_2nd_Input
);

  wire and_1_out, clk, comparison_successor, controlled_buffer_1_out, controlled_buffer_2_out,
       controlled_buffer_5_out, controlled_buffer_6_out, controlled_buffer_12_out, controlled_buffer_13_out,
       counter_5_q, decoder_1_out0, decoder_1_out2, decoder_2_out1, decoder_2_out2, decoder_3_out0,
       decoder_3_out2, decoder_4_out0, decoder_4_out1, decoder_5_out1, decoder_5_out2, is_alu, is_comparison,
       is_immediate, is_jump, jump, jump_branch, jump_j, memRead, memWrite, multiplexer_1_out,
       multiplexer_6_out, next, next_alu, next_ld, next_st, or_1_out, pc_enable, reg_w, reg_w_alu, reg_w_ld,
       register_write_enabled;
  wire [1:0] ALU_OPERATION, counter_2_q, counter_3_q, counter_4_q, counter_6_q;
  wire [3:0] SRC_DEST_OP1;
  wire [9:0] ADDRESS_10;
  wire [13:0] ADDRESS_14;
  wire [17:0] alu_output, data_out, extend14_18_1_out_2, IMM_ADDRESS6, \input , multiplexer_3_out,
       multiplexer_5_out, PC_val, reg1_value, reg2_value, register_write_data, rom_1_data;

  or or_1 (or_1_out, jump, next);
  and and_1 (and_1_out, is_immediate, is_alu);
  Multiplexer #(.enable("false")) multiplexer_1 (.in0(1'b0), .in1(clk), .out(multiplexer_1_out), .sel(or_1_out));
  Clock clock_1 (.out(clk));
  assign controlled_buffer_1_out = pc_enable ? multiplexer_1_out : 1'bz;  // Controlled_Buffer controlled_buffer_1
  Multiplexer #(.width(18), .enable("false")) multiplexer_2 (
    .in0(reg2_value), .in1(IMM_ADDRESS6), .out(ALU_2nd_Input), .sel(and_1_out));
  Counter counter_1 (
    .next(next), .jump(jump), .clk(controlled_buffer_1_out), .\input (\input ), .reset(in_1),
    .\output (PC_val));
  ROM #(.addrWidth(18), .dataWidth(18)) rom_1 (.addr(PC_val), .data(rom_1_data), .sel(1'b1));
  Multiplexer #(.width(18), .enable("false")) multiplexer_3 (
    .in0(18'h1), .in1(IMM_ADDRESS6), .out(multiplexer_3_out), .sel(comparison_successor));
  Control_Unit control_unit_1 (
    ._18_bit_input(rom_1_data), .reg_1_value(reg1_value), .reg_2_value(reg2_value),
    .SRC_DEST_OP1(SRC_DEST_OP1), .SRC1_OP2(read_register_1), .is_immediate(is_immediate),
    .ALU_operation(ALU_OPERATION), .SRC2(read_register_2), .ADDREESS10(ADDRESS_10), .memWrite(memWrite),
    .memRead(memRead), .ADDRESS_14(ADDRESS_14), .is_alu(is_alu), .IMM_ADDRESS6(IMM_ADDRESS6),
    .register_write_enabled(register_write_enabled), .is_comparison(is_comparison),
    .comparison_successor(comparison_successor), .is_jump(is_jump));
  extend14_18 extend14_18_1 (.in_1(ADDRESS_14), .out_2(extend14_18_1_out_2));
  Multiplexer #(.width(18), .enable("false")) multiplexer_4 (
    .in0(multiplexer_3_out), .in1(extend14_18_1_out_2), .out(\input ), .sel(is_jump));
  assign controlled_buffer_2_out = is_alu ? clk : 1'bz;  // Controlled_Buffer controlled_buffer_2
  Multiplexer #(.width(18), .enable("false")) multiplexer_5 (
    .in0(register_write_data), .in1(data_out), .out(multiplexer_5_out), .sel(memRead));
  Counter_part #(.width(2), .max('h2)) counter_2 (
    .Q(counter_2_q), .clk(controlled_buffer_2_out));  // open: load, D, count, carry, clr
  Decoder #(.select(2)) decoder_1 (
    .out0(decoder_1_out0), .out1(reg_w_alu), .out2(decoder_1_out2), .sel(counter_2_q));  // open: out3, en
  assign next_alu = decoder_1_out0 ? 1'b0 : 1'bz;  // Controlled_Buffer controlled_buffer_3
  assign next_alu = decoder_1_out2 ? 1'b1 : 1'bz;  // Controlled_Buffer controlled_buffer_4
  RAM #(.addrWidth(10), .dataWidth(18), .bus("separate")) ram_1 (
    .addr(ADDRESS_10), .din(reg2_value), .data(data_out), .str(memWrite), .sel(1'b1), .clk(clk),
    .ld(memRead), .clr(1'b0));
  Register_file Register (
    .read_register_1(read_register_1), .read_register_2(read_register_2), .Write_register(SRC_DEST_OP1),
    .write_data(multiplexer_5_out), .regWrite(multiplexer_6_out), .in_6(clk), .read_data_1(reg1_value),
    .read_data_2(reg2_value));
  Multiplexer #(.enable("false")) multiplexer_6 (
    .in0(1'b0), .in1(register_write_enabled), .out(multiplexer_6_out), .sel(reg_w));
  assign controlled_buffer_5_out = memRead ? clk : 1'bz;  // Controlled_Buffer controlled_buffer_5
  Counter_part #(.width(2), .max('h2)) counter_3 (
    .Q(counter_3_q), .clk(controlled_buffer_6_out));  // open: load, D, count, carry, clr
  assign controlled_buffer_6_out = is_comparison ? clk : 1'bz;  // Controlled_Buffer controlled_buffer_6
  assign register_write_data = is_alu ? alu_output : 18'bz;  // Controlled_Buffer controlled_buffer_7
  Counter_part #(.width(2), .max('h2)) counter_4 (
    .Q(counter_4_q), .clk(controlled_buffer_5_out));  // open: load, D, count, carry, clr
  Decoder #(.select(2), .enable("false")) decoder_2 (
    .out1(decoder_2_out1), .out2(decoder_2_out2), .sel(counter_3_q));  // open: out0, out3
  ALU alu_1 (.A(reg1_value), .B(ALU_2nd_Input), .ALU_operation(ALU_OPERATION), .result(alu_output));  // open: carry_out
  Decoder #(.select(2), .enable("false")) decoder_3 (
    .out0(decoder_3_out0), .out1(reg_w_ld), .out2(decoder_3_out2), .sel(counter_4_q));  // open: out3
  assign next_ld = decoder_3_out2 ? 1'b1 : 1'bz;  // Controlled_Buffer controlled_buffer_8
  assign jump_branch = decoder_2_out1 ? 1'b1 : 1'bz;  // Controlled_Buffer controlled_buffer_9
  assign jump_branch = decoder_2_out2 ? 1'b0 : 1'bz;  // Controlled_Buffer controlled_buffer_10
  assign next_ld = decoder_3_out0 ? 1'b0 : 1'bz;  // Controlled_Buffer controlled_buffer_11
  assign controlled_buffer_12_out = memWrite ? clk : 1'bz;  // Controlled_Buffer controlled_buffer_12
  assign controlled_buffer_13_out = is_jump ? clk : 1'bz;  // Controlled_Buffer controlled_buffer_13
  or or_2 (pc_enable, next_alu, next_ld, next_st, jump_j, jump_branch);
  or or_3 (next, next_alu, next_ld, next_st);
  Counter_part #(.width(1), .max('h1)) counter_5 (
    .Q(counter_5_q), .clk(controlled_buffer_12_out));  // open: load, D, count, carry, clr
  Counter_part #(.width(2), .max('h2)) counter_6 (
    .Q(counter_6_q), .clk(controlled_buffer_13_out));  // open: load, D, count, carry, clr
  Decoder #(.enable("false")) decoder_4 (.out0(decoder_4_out0), .out1(decoder_4_out1), .sel(counter_5_q));
  assign next_st = decoder_4_out1 ? 1'b1 : 1'bz;  // Controlled_Buffer controlled_buffer_14
  Decoder #(.select(2), .enable("false")) decoder_5 (
    .out1(decoder_5_out1), .out2(decoder_5_out2), .out3(decoder_5_out2), .sel(counter_6_q));  // open: out0
  assign next_st = decoder_4_out0 ? 1'b0 : 1'bz;  // Controlled_Buffer controlled_buffer_15
  assign jump_j = decoder_5_out1 ? 1'b1 : 1'bz;  // Controlled_Buffer controlled_buffer_16
  assign jump_j = decoder_5_out2 ? 1'b0 : 1'bz;  // Controlled_Buffer controlled_buffer_17
  or or_4 (jump, jump_j, jump_branch);
  or or_5 (reg_w, reg_w_alu, reg_w_ld);

  // Other names for the same wires on the sheet: pc_enable_alu = next_alu; pc_enable_branch = jump_branch;
  //   pc_enable_jump = jump_j; pc_enable_ld = next_ld; pc_enable_st = next_st; SRC1_OP2[3:0] = read_register_1;
  //   SRC2[3:0] = read_register_2

  // Notes on the sheet:
  //   immediate ALU ise registerdan 1 tane deger oku
  //   diger degeri de  CU'dan al ve ALU'ya gonder
  //   contents of rom_1 (hex, n*v repeats v):
  //   4848 c9c 1fb7b 9158 104d0 55bc f3f9 15e06 191e0 20805 24c0f 28011 3627c 387c3 3c8c8 2d9f7 32251
  //   3e27e
  //   eğer karşılaştırma koşulu sağlanıyorsa adresi gönder, sağlanmıyorsa +1
  //   jump opcode geldiyse address_14'ü extend edip counter'a gönder
  //   ALU FSM
  //   DATA MEMORY
  //   BRANCH
  //   LD FSM
  //   JUMP
  //   ST FSM
endmodule

module d_latch (
  input  D,
  input  clk,
  output Q_prime,
  output Q
);

  wire and_1_out, and_2_out, not_1_out;

  and and_1 (and_1_out, D, clk);
  and and_2 (and_2_out, clk, not_1_out);
  not not_1 (not_1_out, D);
  nor nor_1 (Q_prime, and_1_out, Q);
  nor nor_2 (Q, Q_prime, and_2_out);
endmodule

module d_FlipFlop (
  input  D,
  input  clk,
  output out_3
);

  wire master_q, not_1_out;

  not not_1 (not_1_out, clk);
  d_latch master (.D(D), .clk(not_1_out), .Q(master_q));  // open: Q_prime
  d_latch servant (.D(master_q), .clk(clk), .Q(out_3));  // open: Q_prime
endmodule

module extend6_18 (
  input  [5:0] in_1,
  output [17:0] out_2
);

  Multiplexer #(.width(12), .enable("false")) multiplexer_1 (
    .in0({12{1'b0}}), .in1({12{1'b1}}), .out(out_2[17:6]), .sel(in_1[5]));

  assign out_2[5:0] = in_1;

  // Other names for the same wires on the sheet: val[4:0] = in_1[4:0]; sign = in_1[5];
  //   extend_bits[11:0] = out_2[17:6]
endmodule

module extend10_18 (
  input  [9:0] in_1,
  output [17:0] out_2
);

  Multiplexer #(.width(8), .enable("false")) multiplexer_1 (
    .in0({8{1'b0}}), .in1({8{1'b1}}), .out(out_2[17:10]), .sel(in_1[9]));

  assign out_2[9:0] = in_1;

  // Other names for the same wires on the sheet: val[8:0] = in_1[8:0]; sign = in_1[9];
  //   extend_bits[7:0] = out_2[17:10]
endmodule

module extend14_18 (
  input  [13:0] in_1,
  output [17:0] out_2
);

  Multiplexer #(.width(4), .enable("false")) multiplexer_1 (
    .in0(4'b0000), .in1(4'b1111), .out(out_2[17:14]), .sel(in_1[13]));

  assign out_2[13:0] = in_1;

  // Other names for the same wires on the sheet: val[12:0] = in_1[12:0]; sign = in_1[13];
  //   extend_bits[3:0] = out_2[17:14]
endmodule

module half_comparator (
  input  A,
  input  B,
  output gt,
  output lt,
  output eq
);

  wire and_1_out, and_4_out, not_1_out, not_2_out, not_3_out, not_4_out;

  not not_1 (not_1_out, A);
  and and_1 (and_1_out, not_1_out, not_2_out);
  not not_2 (not_2_out, B);
  and and_2 (gt, A, not_3_out);
  not not_3 (not_3_out, B);
  not not_4 (not_4_out, A);
  and and_3 (lt, not_4_out, B);
  and and_4 (and_4_out, A, B);
  or or_1 (eq, and_4_out, and_1_out);
endmodule

module full_comparator (
  input  a,
  input  b,
  input  gt_in,
  input  lt_in,
  input  eq_in,
  output gt,
  output lt,
  output eq
);

  wire and_1_out, and_2_out, and_3_out, and_4_out, and_5_out, and_6_out, not_1_out, not_2_out, not_3_out,
       not_4_out, or_1_out;

  not not_1 (not_1_out, b);
  not not_2 (not_2_out, a);
  and and_1 (and_1_out, a, b);
  not not_3 (not_3_out, a);
  and and_2 (and_2_out, not_3_out, not_4_out);
  not not_4 (not_4_out, b);
  and and_3 (and_3_out, a, not_1_out);
  and and_4 (and_4_out, and_3_out, eq_in);
  and and_5 (and_5_out, eq_in, and_6_out);
  and and_6 (and_6_out, not_2_out, b);
  or or_1 (or_1_out, and_1_out, and_2_out);
  or or_2 (gt, and_4_out, gt_in);
  or or_3 (lt, and_5_out, lt_in);
  and and_7 (eq, eq_in, or_1_out);
endmodule

module _4_bits_comparator (
  input  [3:0] a,
  input  [3:0] b,
  output gt,
  output lt,
  output eq
);

  wire full_comparator_1_eq, full_comparator_1_gt, full_comparator_1_lt, full_comparator_2_eq,
       full_comparator_2_gt, full_comparator_2_lt, half_comparator_1_eq, half_comparator_1_gt,
       half_comparator_1_lt;

  half_comparator half_comparator_1 (
    .A(a[3]), .B(b[3]), .gt(half_comparator_1_gt), .lt(half_comparator_1_lt), .eq(half_comparator_1_eq));
  full_comparator full_comparator_1 (
    .a(a[2]), .b(b[2]), .gt_in(half_comparator_1_gt), .lt_in(half_comparator_1_lt),
    .eq_in(half_comparator_1_eq), .gt(full_comparator_1_gt), .lt(full_comparator_1_lt),
    .eq(full_comparator_1_eq));
  full_comparator full_comparator_2 (
    .a(a[1]), .b(b[1]), .gt_in(full_comparator_1_gt), .lt_in(full_comparator_1_lt),
    .eq_in(full_comparator_1_eq), .gt(full_comparator_2_gt), .lt(full_comparator_2_lt),
    .eq(full_comparator_2_eq));
  full_comparator full_comparator_3 (
    .a(a[0]), .b(b[0]), .gt_in(full_comparator_2_gt), .lt_in(full_comparator_2_lt),
    .eq_in(full_comparator_2_eq), .gt(gt), .lt(lt), .eq(eq));

  // Other names for the same wires on the sheet: a_0 = a[0]; a_1 = a[1]; a_2 = a[2]; a_3 = a[3]; b_0 = b[0];
  //   b_1 = b[1]; b_2 = b[2]; b_3 = b[3]
endmodule

module _18_bits_comparator (
  input  [17:0] a,
  input  [17:0] b,
  output gt,
  output lt,
  output eq
);

  wire full_comparator_1_eq, full_comparator_1_gt, full_comparator_1_lt, full_comparator_2_eq,
       full_comparator_2_gt, full_comparator_2_lt, full_comparator_3_eq, full_comparator_3_gt,
       full_comparator_3_lt, full_comparator_4_eq, full_comparator_4_gt, full_comparator_4_lt,
       full_comparator_5_eq, full_comparator_5_gt, full_comparator_5_lt, full_comparator_6_eq,
       full_comparator_6_gt, full_comparator_6_lt, full_comparator_7_eq, full_comparator_7_gt,
       full_comparator_7_lt, full_comparator_8_eq, full_comparator_8_gt, full_comparator_8_lt,
       full_comparator_9_eq, full_comparator_9_gt, full_comparator_9_lt, full_comparator_10_eq,
       full_comparator_10_gt, full_comparator_10_lt, full_comparator_11_eq, full_comparator_11_gt,
       full_comparator_11_lt, full_comparator_12_eq, full_comparator_12_gt, full_comparator_12_lt,
       full_comparator_13_eq, full_comparator_13_gt, full_comparator_13_lt, full_comparator_14_eq,
       full_comparator_14_gt, full_comparator_14_lt, full_comparator_15_eq, full_comparator_15_gt,
       full_comparator_15_lt, full_comparator_16_eq, full_comparator_16_gt, full_comparator_16_lt,
       half_comparator_1_eq, half_comparator_1_gt, half_comparator_1_lt;

  half_comparator half_comparator_1 (
    .A(a[17]), .B(b[17]), .gt(half_comparator_1_gt), .lt(half_comparator_1_lt), .eq(half_comparator_1_eq));
  full_comparator full_comparator_1 (
    .a(a[8]), .b(b[8]), .gt_in(full_comparator_16_gt), .lt_in(full_comparator_16_lt),
    .eq_in(full_comparator_16_eq), .gt(full_comparator_1_gt), .lt(full_comparator_1_lt),
    .eq(full_comparator_1_eq));
  full_comparator full_comparator_2 (
    .a(a[16]), .b(b[16]), .gt_in(half_comparator_1_gt), .lt_in(half_comparator_1_lt),
    .eq_in(half_comparator_1_eq), .gt(full_comparator_2_gt), .lt(full_comparator_2_lt),
    .eq(full_comparator_2_eq));
  full_comparator full_comparator_3 (
    .a(a[7]), .b(b[7]), .gt_in(full_comparator_1_gt), .lt_in(full_comparator_1_lt),
    .eq_in(full_comparator_1_eq), .gt(full_comparator_3_gt), .lt(full_comparator_3_lt),
    .eq(full_comparator_3_eq));
  full_comparator full_comparator_4 (
    .a(a[15]), .b(b[15]), .gt_in(full_comparator_2_gt), .lt_in(full_comparator_2_lt),
    .eq_in(full_comparator_2_eq), .gt(full_comparator_4_gt), .lt(full_comparator_4_lt),
    .eq(full_comparator_4_eq));
  full_comparator full_comparator_5 (
    .a(a[14]), .b(b[14]), .gt_in(full_comparator_4_gt), .lt_in(full_comparator_4_lt),
    .eq_in(full_comparator_4_eq), .gt(full_comparator_5_gt), .lt(full_comparator_5_lt),
    .eq(full_comparator_5_eq));
  full_comparator full_comparator_6 (
    .a(a[6]), .b(b[6]), .gt_in(full_comparator_3_gt), .lt_in(full_comparator_3_lt),
    .eq_in(full_comparator_3_eq), .gt(full_comparator_6_gt), .lt(full_comparator_6_lt),
    .eq(full_comparator_6_eq));
  full_comparator full_comparator_7 (
    .a(a[13]), .b(b[13]), .gt_in(full_comparator_5_gt), .lt_in(full_comparator_5_lt),
    .eq_in(full_comparator_5_eq), .gt(full_comparator_7_gt), .lt(full_comparator_7_lt),
    .eq(full_comparator_7_eq));
  full_comparator full_comparator_8 (
    .a(a[5]), .b(b[5]), .gt_in(full_comparator_6_gt), .lt_in(full_comparator_6_lt),
    .eq_in(full_comparator_6_eq), .gt(full_comparator_8_gt), .lt(full_comparator_8_lt),
    .eq(full_comparator_8_eq));
  full_comparator full_comparator_9 (
    .a(a[12]), .b(b[12]), .gt_in(full_comparator_7_gt), .lt_in(full_comparator_7_lt),
    .eq_in(full_comparator_7_eq), .gt(full_comparator_9_gt), .lt(full_comparator_9_lt),
    .eq(full_comparator_9_eq));
  full_comparator full_comparator_10 (
    .a(a[4]), .b(b[4]), .gt_in(full_comparator_8_gt), .lt_in(full_comparator_8_lt),
    .eq_in(full_comparator_8_eq), .gt(full_comparator_10_gt), .lt(full_comparator_10_lt),
    .eq(full_comparator_10_eq));
  full_comparator full_comparator_11 (
    .a(a[11]), .b(b[11]), .gt_in(full_comparator_9_gt), .lt_in(full_comparator_9_lt),
    .eq_in(full_comparator_9_eq), .gt(full_comparator_11_gt), .lt(full_comparator_11_lt),
    .eq(full_comparator_11_eq));
  full_comparator full_comparator_12 (
    .a(a[3]), .b(b[3]), .gt_in(full_comparator_10_gt), .lt_in(full_comparator_10_lt),
    .eq_in(full_comparator_10_eq), .gt(full_comparator_12_gt), .lt(full_comparator_12_lt),
    .eq(full_comparator_12_eq));
  full_comparator full_comparator_13 (
    .a(a[10]), .b(b[10]), .gt_in(full_comparator_11_gt), .lt_in(full_comparator_11_lt),
    .eq_in(full_comparator_11_eq), .gt(full_comparator_13_gt), .lt(full_comparator_13_lt),
    .eq(full_comparator_13_eq));
  full_comparator full_comparator_14 (
    .a(a[2]), .b(b[2]), .gt_in(full_comparator_12_gt), .lt_in(full_comparator_12_lt),
    .eq_in(full_comparator_12_eq), .gt(full_comparator_14_gt), .lt(full_comparator_14_lt),
    .eq(full_comparator_14_eq));
  full_comparator full_comparator_15 (
    .a(a[1]), .b(b[1]), .gt_in(full_comparator_14_gt), .lt_in(full_comparator_14_lt),
    .eq_in(full_comparator_14_eq), .gt(full_comparator_15_gt), .lt(full_comparator_15_lt),
    .eq(full_comparator_15_eq));
  full_comparator full_comparator_16 (
    .a(a[9]), .b(b[9]), .gt_in(full_comparator_13_gt), .lt_in(full_comparator_13_lt),
    .eq_in(full_comparator_13_eq), .gt(full_comparator_16_gt), .lt(full_comparator_16_lt),
    .eq(full_comparator_16_eq));
  full_comparator full_comparator_17 (
    .a(a[0]), .b(b[0]), .gt_in(full_comparator_15_gt), .lt_in(full_comparator_15_lt),
    .eq_in(full_comparator_15_eq), .gt(gt), .lt(lt), .eq(eq));

  // Other names for the same wires on the sheet: a_0 = a[0]; a_1 = a[1]; a_2 = a[2]; a_3 = a[3]; a_4 = a[4];
  //   a_5 = a[5]; a_6 = a[6]; a_7 = a[7]; a_8 = a[8]; a_9 = a[9]; a_10 = a[10]; a_11 = a[11]; a_12 = a[12];
  //   a_13 = a[13]; a_14 = a[14]; a_15 = a[15]; a_16 = a[16]; a_17 = a[17]; b_0 = b[0]; b_1 = b[1]; b_2 = b[2];
  //   b_3 = b[3]; b_4 = b[4]; b_5 = b[5]; b_6 = b[6]; b_7 = b[7]; b_8 = b[8]; b_9 = b[9]; b_10 = b[10]; b_11 = b[11];
  //   b_12 = b[12]; b_13 = b[13]; b_14 = b[14]; b_15 = b[15]; b_16 = b[16]; b_17 = b[17]
endmodule

module _18_bits_inverter (
  input  [17:0] in_1,
  output [17:0] out_2
);

  wire [17:0] negator_1_out;

  Negator #(.width(18)) negator_1 (.in(in_1), .out(negator_1_out));
  Multiplexer #(.width(18)) multiplexer_1 (.in0(in_1), .in1(negator_1_out), .out(out_2), .sel(in_1[17]));  // open: en
endmodule

module _18_bits_adder (
  input  [17:0] A,
  input  [17:0] B,
  input  carry_in,
  output carry_out,
  output [17:0] sum
);

  wire n2_bits_adder_1_carry_out, n2_bits_adder_2_carry_out, n2_bits_adder_3_carry_out,
       n2_bits_adder_4_carry_out, n2_bits_adder_5_carry_out, n2_bits_adder_6_carry_out,
       n2_bits_adder_7_carry_out, n2_bits_adder_8_carry_out;

  _2_bits_adder u_2_bits_adder_1 (
    .A(A[1:0]), .B(B[1:0]), .carry_in(carry_in), .carry_out(n2_bits_adder_1_carry_out), .sum(sum[1:0]));
  _2_bits_adder u_2_bits_adder_2 (
    .A(A[3:2]), .B(B[3:2]), .carry_in(n2_bits_adder_1_carry_out), .carry_out(n2_bits_adder_2_carry_out),
    .sum(sum[3:2]));
  _2_bits_adder u_2_bits_adder_3 (
    .A(A[5:4]), .B(B[5:4]), .carry_in(n2_bits_adder_2_carry_out), .carry_out(n2_bits_adder_3_carry_out),
    .sum(sum[5:4]));
  _2_bits_adder u_2_bits_adder_4 (
    .A(A[7:6]), .B(B[7:6]), .carry_in(n2_bits_adder_3_carry_out), .carry_out(n2_bits_adder_4_carry_out),
    .sum(sum[7:6]));
  _2_bits_adder u_2_bits_adder_5 (
    .A(A[11:10]), .B(B[11:10]), .carry_in(n2_bits_adder_6_carry_out), .carry_out(n2_bits_adder_5_carry_out),
    .sum(sum[11:10]));
  _2_bits_adder u_2_bits_adder_6 (
    .A(A[9:8]), .B(B[9:8]), .carry_in(n2_bits_adder_4_carry_out), .carry_out(n2_bits_adder_6_carry_out),
    .sum(sum[9:8]));
  _2_bits_adder u_2_bits_adder_7 (
    .A(A[13:12]), .B(B[13:12]), .carry_in(n2_bits_adder_5_carry_out), .carry_out(n2_bits_adder_7_carry_out),
    .sum(sum[13:12]));
  _2_bits_adder u_2_bits_adder_8 (
    .A(A[15:14]), .B(B[15:14]), .carry_in(n2_bits_adder_7_carry_out), .carry_out(n2_bits_adder_8_carry_out),
    .sum(sum[15:14]));
  _2_bits_adder u_2_bits_adder_9 (
    .A(A[17:16]), .B(B[17:16]), .carry_in(n2_bits_adder_8_carry_out), .carry_out(carry_out), .sum(sum[17:16]));
endmodule

module _8_bits_adder (
  input  [7:0] A,
  input  [7:0] B,
  input  carry_in,
  output carry_out,
  output [7:0] sum
);

  wire n4_bits_adder_1_carry_out;

  _4_bits_adder u_4_bits_adder_1 (
    .A(A[3:0]), .B(B[3:0]), .carry_in(carry_in), .carry_out(n4_bits_adder_1_carry_out), .sum(sum[3:0]));
  _4_bits_adder u_4_bits_adder_2 (
    .A(A[7:4]), .B(B[7:4]), .carry_in(n4_bits_adder_1_carry_out), .carry_out(carry_out), .sum(sum[7:4]));
endmodule

module _4_bits_adder (
  input  [3:0] A,
  input  [3:0] B,
  input  carry_in,
  output carry_out,
  output [3:0] sum
);

  wire full_adder_1_carry_out, full_adder_2_carry_out, full_adder_3_carry_out;

  full_adder full_adder_1 (.A(A[0]), .B(B[0]), .carry_in(carry_in), .sum(sum[0]), .carry_out(full_adder_1_carry_out));
  full_adder full_adder_2 (
    .A(A[1]), .B(B[1]), .carry_in(full_adder_1_carry_out), .sum(sum[1]), .carry_out(full_adder_2_carry_out));
  full_adder full_adder_3 (
    .A(A[2]), .B(B[2]), .carry_in(full_adder_2_carry_out), .sum(sum[2]), .carry_out(full_adder_3_carry_out));
  full_adder full_adder_4 (.A(A[3]), .B(B[3]), .carry_in(full_adder_3_carry_out), .sum(sum[3]), .carry_out(carry_out));
endmodule

module _2_bits_adder (
  input  [1:0] A,
  input  [1:0] B,
  input  carry_in,
  output carry_out,
  output [1:0] sum
);

  wire full_adder_1_carry_out;

  full_adder full_adder_1 (.A(A[0]), .B(B[0]), .carry_in(carry_in), .sum(sum[0]), .carry_out(full_adder_1_carry_out));
  full_adder full_adder_2 (.A(A[1]), .B(B[1]), .carry_in(full_adder_1_carry_out), .sum(sum[1]), .carry_out(carry_out));
endmodule

module full_adder (
  input  A,
  input  B,
  input  carry_in,
  output sum,
  output carry_out
);

  wire and_1_out, and_2_out, xor_1_out;

  xor xor_1 (xor_1_out, A, B);
  xor xor_2 (sum, xor_1_out, carry_in);
  and and_1 (and_1_out, carry_in, xor_1_out);
  and and_2 (and_2_out, B, A);
  or or_1 (carry_out, and_1_out, and_2_out);
endmodule

// PC
module Counter (
  input  next,
  input  jump,
  input  clk,
  input  [17:0] \input ,
  input  reset,
  output [17:0] \output 
);

  wire load_enable, not_1_out, or_1_out;
  wire [17:0] added_value, n18_bits_inverter_1_out_2, substracted_value, value_to_load;

  not not_1 (not_1_out, next);
  and and_1 (load_enable, not_1_out, or_1_out);
  or or_1 (or_1_out, jump, \input [17]);
  Counter_part #(.width(18), .max('h3ffff)) counter_1 (
    .load(load_enable), .D(value_to_load), .count(next), .Q(\output ), .clk(clk), .clr(reset));  // open: carry
  _18_bits_inverter u_18_bits_inverter_1 (.in_1(\input ), .out_2(n18_bits_inverter_1_out_2));
  Adder #(.width(18)) adder_1 (.a(\input ), .b(\output ), .out(added_value));  // open: cin, cout
  Subtractor #(.width(18)) subtractor_1 (
    .a(\output ), .b(n18_bits_inverter_1_out_2), .out(substracted_value));  // open: bin, bout
  assign value_to_load = jump ? added_value : 18'bz;  // Controlled_Buffer controlled_buffer_1
  assign value_to_load = \input [17] ? substracted_value : 18'bz;  // Controlled_Buffer controlled_buffer_2

  // Other names for the same wires on the sheet: count = next; substract = \input [17]

  // Notes on the sheet:
  //   increment by 1 (count=1, clock ticks)
endmodule

module ALU (
  input  [17:0] A,
  input  [17:0] B,
  input  [1:0] ALU_operation,
  output [17:0] result,
  output carry_out
);

  wire [17:0] AND_out, n18_bits_adder_1_sum, OR_out, XOR_out;

  _18_bits_adder u_18_bits_adder_1 (.A(A), .B(B), .carry_in(1'b0), .carry_out(carry_out), .sum(n18_bits_adder_1_sum));
  assign AND_out = B & A;  // AND_Gate AND, 18 bits wide
  assign OR_out = B | A;  // OR_Gate OR, 18 bits wide
  assign XOR_out = A ^ B;  // XOR_Gate XOR, 18 bits wide
  Multiplexer #(.select(2), .width(18), .enable("false")) multiplexer_1 (
    .in0(n18_bits_adder_1_sum), .in1(AND_out), .in2(OR_out), .in3(XOR_out), .out(result), .sel(ALU_operation));
endmodule

module Register_file (
  input  [3:0] read_register_1,
  input  [3:0] read_register_2,
  input  [3:0] Write_register,
  input  [17:0] write_data,
  input  regWrite,
  input  in_6,
  output [17:0] read_data_1,
  output [17:0] read_data_2
);

  wire and_1_out, and_2_out, and_3_out, and_4_out, and_5_out, and_6_out, and_7_out, and_8_out, and_9_out,
       and_10_out, and_11_out, and_12_out, and_13_out, and_14_out, and_15_out, and_16_out, decoder_1_out0,
       decoder_1_out1, decoder_1_out2, decoder_1_out3, decoder_1_out4, decoder_1_out5, decoder_1_out6,
       decoder_1_out7, decoder_1_out8, decoder_1_out9, decoder_1_out10, decoder_1_out11, decoder_1_out12,
       decoder_1_out13, decoder_1_out14, decoder_1_out15;
  wire [17:0] R0_q, R1_q, R2_q, R3_q, R4_q, R5_q, R6_q, R7_q, R8_q, R9_q, R10_q, R11_q, R12_q, R13_q, R14_q,
       R15_q;

  Decoder #(.select(4), .enable("false")) decoder_1 (
    .out0(decoder_1_out0), .out1(decoder_1_out1), .out2(decoder_1_out2), .out3(decoder_1_out3),
    .out4(decoder_1_out4), .out5(decoder_1_out5), .out6(decoder_1_out6), .out7(decoder_1_out7),
    .out8(decoder_1_out8), .out9(decoder_1_out9), .out10(decoder_1_out10), .out11(decoder_1_out11),
    .out12(decoder_1_out12), .out13(decoder_1_out13), .out14(decoder_1_out14), .out15(decoder_1_out15),
    .sel(Write_register));
  and and_1 (and_1_out, regWrite, decoder_1_out0);
  and and_2 (and_2_out, regWrite, decoder_1_out1);
  and and_3 (and_3_out, regWrite, decoder_1_out2);
  and and_4 (and_4_out, regWrite, decoder_1_out3);
  and and_5 (and_5_out, regWrite, decoder_1_out4);
  and and_6 (and_6_out, regWrite, decoder_1_out5);
  and and_7 (and_7_out, regWrite, decoder_1_out6);
  and and_8 (and_8_out, regWrite, decoder_1_out7);
  Register #(.width(18)) R0 (.D(write_data), .en(and_1_out), .Q(R0_q), .clk(in_6));  // open: clr
  Register #(.width(18)) R1 (.D(write_data), .en(and_2_out), .Q(R1_q), .clk(in_6));  // open: clr
  Register #(.width(18)) R2 (.D(write_data), .en(and_3_out), .Q(R2_q), .clk(in_6));  // open: clr
  Register #(.width(18)) R3 (.D(write_data), .en(and_4_out), .Q(R3_q), .clk(in_6));  // open: clr
  Register #(.width(18)) R4 (.D(write_data), .en(and_5_out), .Q(R4_q), .clk(in_6));  // open: clr
  Register #(.width(18)) R5 (.D(write_data), .en(and_6_out), .Q(R5_q), .clk(in_6));  // open: clr
  Register #(.width(18)) R6 (.D(write_data), .en(and_7_out), .Q(R6_q), .clk(in_6));  // open: clr
  Register #(.width(18)) R7 (.D(write_data), .en(and_8_out), .Q(R7_q), .clk(in_6));  // open: clr
  and and_9 (and_9_out, regWrite, decoder_1_out8);
  and and_10 (and_10_out, regWrite, decoder_1_out9);
  and and_11 (and_11_out, regWrite, decoder_1_out10);
  and and_12 (and_12_out, regWrite, decoder_1_out11);
  and and_13 (and_13_out, regWrite, decoder_1_out12);
  and and_14 (and_14_out, regWrite, decoder_1_out13);
  and and_15 (and_15_out, regWrite, decoder_1_out14);
  and and_16 (and_16_out, regWrite, decoder_1_out15);
  Register #(.width(18)) R8 (.D(write_data), .en(and_9_out), .Q(R8_q), .clk(in_6));  // open: clr
  Register #(.width(18)) R9 (.D(write_data), .en(and_10_out), .Q(R9_q), .clk(in_6));  // open: clr
  Register #(.width(18)) R10 (.D(write_data), .en(and_11_out), .Q(R10_q), .clk(in_6));  // open: clr
  Register #(.width(18)) R11 (.D(write_data), .en(and_12_out), .Q(R11_q), .clk(in_6));  // open: clr
  Register #(.width(18)) R12 (.D(write_data), .en(and_13_out), .Q(R12_q), .clk(in_6));  // open: clr
  Register #(.width(18)) R13 (.D(write_data), .en(and_14_out), .Q(R13_q), .clk(in_6));  // open: clr
  Register #(.width(18)) R14 (.D(write_data), .en(and_15_out), .Q(R14_q), .clk(in_6));  // open: clr
  Register #(.width(18)) R15 (.D(write_data), .en(and_16_out), .Q(R15_q), .clk(in_6));  // open: clr
  Multiplexer #(.select(4), .width(18), .enable("false")) multiplexer_1 (
    .in0(R0_q), .in1(R1_q), .in2(R2_q), .in3(R3_q), .in4(R4_q), .in5(R5_q), .in6(R6_q), .in7(R7_q),
    .in8(R8_q), .in9(R9_q), .in10(R10_q), .in11(R11_q), .in12(R12_q), .in13(R13_q), .in14(R14_q),
    .in15(R15_q), .out(read_data_1), .sel(read_register_1));
  Multiplexer #(.select(4), .width(18), .enable("false")) multiplexer_2 (
    .in0(R0_q), .in1(R1_q), .in2(R2_q), .in3(R3_q), .in4(R4_q), .in5(R5_q), .in6(R6_q), .in7(R7_q),
    .in8(R8_q), .in9(R9_q), .in10(R10_q), .in11(R11_q), .in12(R12_q), .in13(R13_q), .in14(R14_q),
    .in15(R15_q), .out(read_data_2), .sel(read_register_2));
endmodule

// ControlUnit
module Control_Unit (
  input  [17:0] _18_bit_input,
  input  [17:0] reg_1_value,
  input  [17:0] reg_2_value,
  output [3:0] SRC_DEST_OP1,
  output [3:0] SRC1_OP2,
  output is_immediate,
  output [1:0] ALU_operation,
  output [3:0] SRC2,
  output [9:0] ADDREESS10,
  output memWrite,
  output memRead,
  output [13:0] ADDRESS_14,
  output is_alu,
  output [17:0] IMM_ADDRESS6,
  output register_write_enabled,
  output is_comparison,
  output comparison_successor,
  output is_jump
);

  wire ADD, ADDI, AND, and_1_out, and_2_out, and_3_out, and_4_out, and_5_out, ANDI, BEQ, BGE, BGT, BLE, BLT,
       n18_bits_comparator_1_eq, n18_bits_comparator_1_gt, n18_bits_comparator_1_lt, OR, or_1_out, or_2_out,
       or_3_out, or_4_out, or_5_out, or_6_out, ORI, XOR, XORI;

  assign IMM_ADDRESS6 = {{12{_18_bit_input[5]}}, _18_bit_input[5:0]};  // Bit_Extender bit_extender_1
  Decoder #(.select(4)) decoder_1 (
    .out0(ADD), .out1(ADDI), .out2(AND), .out3(ANDI), .out4(OR), .out5(ORI), .out6(XOR), .out7(XORI),
    .out8(memRead), .out9(memWrite), .out10(is_jump), .out11(BEQ), .out12(BLT), .out13(BGT), .out14(BGE),
    .out15(BLE), .sel(_18_bit_input[17:14]), .en(1'b1));
  _18_bits_comparator u_18_bits_comparator_1 (
    .a(reg_1_value), .b(reg_2_value), .gt(n18_bits_comparator_1_gt), .lt(n18_bits_comparator_1_lt),
    .eq(n18_bits_comparator_1_eq));
  or or_1 (or_1_out, ADD, ADDI);
  or or_2 (or_2_out, AND, ANDI);
  or or_3 (or_3_out, OR, ORI);
  or or_4 (or_4_out, XOR, XORI);
  or or_5 (or_5_out, n18_bits_comparator_1_eq, n18_bits_comparator_1_gt);
  or or_6 (or_6_out, n18_bits_comparator_1_eq, n18_bits_comparator_1_lt);
  or or_7 (register_write_enabled, is_alu, memRead);
  and and_1 (and_1_out, BGE, or_5_out);
  and and_2 (and_2_out, BLE, or_6_out);
  and and_3 (and_3_out, BGT, n18_bits_comparator_1_gt);
  and and_4 (and_4_out, BLT, n18_bits_comparator_1_lt);
  and and_5 (and_5_out, BEQ, n18_bits_comparator_1_eq);
  Priority_Encoder #(.select(2)) priority_encoder_1 (
    .in0(or_1_out), .in1(or_2_out), .in2(or_3_out), .in3(or_4_out), .out(ALU_operation));  // open: gs, en_out, en_in
  or or_8 (is_alu, or_1_out, or_2_out, or_3_out, or_4_out);
  or or_9 (comparison_successor, and_1_out, and_2_out, and_3_out, and_4_out, and_5_out);
  or or_10 (is_immediate, ADDI, ANDI, ORI, XORI);
  or or_11 (is_comparison, BEQ, BLT, BGT, BGE, BLE);

  assign ADDREESS10 = _18_bit_input[9:0];
  assign ADDRESS_14 = _18_bit_input[13:0];
  assign SRC1_OP2 = _18_bit_input[9:6];
  assign SRC2 = _18_bit_input[5:2];
  assign SRC_DEST_OP1 = _18_bit_input[13:10];

  // Other names for the same wires on the sheet: ADDRESS6[5:0] = _18_bit_input[5:0];
  //   ADDRESS10[9:0] = _18_bit_input[9:0]; ADDRESS14[13:0] = _18_bit_input[13:0]; IMM[5:0] = _18_bit_input[5:0];
  //   OP2[3:0] = _18_bit_input[9:6]; SRC1[3:0] = _18_bit_input[9:6]; ALU_CONTROL = is_alu; JUMP = is_jump;
  //   LD = memRead; OPCODE[3:0] = _18_bit_input[17:14]; DEST[3:0] = _18_bit_input[13:10];
  //   OP1[3:0] = _18_bit_input[13:10]; SRC[3:0] = _18_bit_input[13:10]; ST = memWrite

  // Notes on the sheet:
  //   First 2 bits are useless
  //   Instruction ST ise memWrite sinyali üret
  //   opcode'a karşılık gelen işlem sağlanıyorsa successor 1, değilse 0
  //   çıktı ALU'daki select pin'e bağlanacak
  //   hangi işlemin yapılacağını belirleyecek
  //   (tum aritmetik islemler ve LD )
endmodule
