// Logisim project ControlUnit.circ as structural Verilog
module ControlUnit (
  input  [19:0] in_1,
  output [1:0] ALU_operation
);

  wire ADD, ADDI, ALU_CONTROL, AND, ANDI, BEQ, BGE, BGT, BLE, BLT, JUMP, LD, OR, or_1_out, or_2_out,
       or_3_out, or_4_out, ORI, ST, XOR, XORI;

  Decoder #(.select(4)) decoder_1 (
    .out0(ADD), .out1(ADDI), .out2(AND), .out3(ANDI), .out4(OR), .out5(ORI), .out6(XOR), .out7(XORI),
    .out8(LD), .out9(ST), .out10(JUMP), .out11(BEQ), .out12(BLT), .out13(BGT), .out14(BGE), .out15(BLE),
    .sel(in_1[17:14]), .en(1'b1));
  or or_1 (or_1_out, ADD, ADDI);
  or or_2 (or_2_out, AND, ANDI);
  or or_3 (or_3_out, OR, ORI);
  or or_4 (or_4_out, XOR, XORI);
  Priority_Encoder #(.select(2)) priority_encoder_1 (
    .in0(or_1_out), .in1(or_2_out), .in2(or_3_out), .in3(or_4_out), .out(ALU_operation));  // open: gs, en_out, en_in
  or or_5 (ALU_CONTROL, or_1_out, or_2_out, or_3_out, or_4_out);

  // Other names for the same wires on the sheet: ADDRESS6[5:0] = in_1[5:0]; ADDRESS10[9:0] = in_1[9:0];
  //   ADDRESS14[13:0] = in_1[13:0]; IMM[5:0] = in_1[5:0]; SRC2[3:0] = in_1[5:2]; OP2[3:0] = in_1[9:6];
  //   SRC1[3:0] = in_1[9:6]; OPCODE[3:0] = in_1[17:14]; DEST[3:0] = in_1[13:10]; OP1[3:0] = in_1[13:10];
  //   SRC[3:0] = in_1[13:10]

  // Notes on the sheet:
  //   First 2 bits are useless
  //   çıktı ALU'daki select pin'e bağlanacak
  //   hangi işlemin yapılacağını belirleyecek
endmodule
